// Logisim project automatic_street_light.circ as structural Verilog: 1 circuit, main circuit main
module main (
  input  D,
  input  M,
  input  E,
  output L
);

  wire not_1_out, or_1_out;

  not not_1 (not_1_out, D);
  or or_1 (or_1_out, not_1_out, M);
  and and_1 (L, or_1_out, E);
  LED STREET_LIGHT (.in(L));
endmodule
